# Fritzing sketch Robot-Fritzing (saved by Fritzing 0.9.2b)
breadboards: 1

parts:
  Part1 = Arduino Mega 2560 (Rev3)
  LED1 = RGB LED (com. cathode, rbg) [package="5 mm [THT]"]
  LED2 = RGB LED (com. cathode, rbg) [package="5 mm [THT]"]
  LED3 = RGB LED (com. cathode, rbg) [package="5 mm [THT]"]
  LED4 = RGB LED (com. cathode, rbg) [package="5 mm [THT]"]

nets:
  N1: Part1.D13_PWM, LED1.red_anode
  N2: Part1.D12_PWM, LED1.common_cathode
  N3: Part1.D11_PWM, LED1.green_anode
  N4: Part1.D10_PWM, LED2.red_anode
  N5: Part1.D9_PWM, LED2.common_cathode
  N6: Part1.D8_PWM, LED2.green_anode
  N7: Part1.3V3, LED1.blue_anode, LED2.blue_anode, LED3.blue_anode
  N8: Part1.D2_PWM, LED4.green_anode
  N9: Part1.D3_PWM, LED4.common_cathode
  N10: Part1.D4_PWM, LED4.red_anode
  N11: Part1.D5_PWM, LED3.green_anode
  N12: Part1.D6_PWM, LED3.common_cathode
  N13: Part1.D7_PWM, LED3.red_anode
